// Logisim project CPU-16Bit.circ as structural Verilog: 5 circuits, main circuit ALU
module ALU (
  input  [15:0] Input1,
  input  LoadImm,
  input  [15:0] Input2,
  input  [1:0] ALUOp,
  input  BranchType,
  output [15:0] Result,
  output BranchCond
);

  wire comparator_1_eq, comparator_1_lt, not_1_out, or_2_out;
  wire [15:0] adder_1_out, and_1_out, multiplexer_1_out, or_1_out;

  Multiplexer #(.width(16), .enable("false")) multiplexer_1 (
    .in0(Input1), .in1({16{1'b0}}), .out(multiplexer_1_out), .sel(LoadImm));
  Adder #(.width(16)) adder_1 (.a(multiplexer_1_out), .b(Input2), .out(adder_1_out));  // open: cin, cout
  assign or_1_out = multiplexer_1_out | Input2;  // OR_Gate or_1, 16 bits wide
  assign and_1_out = multiplexer_1_out & Input2;  // AND_Gate and_1, 16 bits wide
  Comparator #(.width(16)) comparator_1 (
    .a(multiplexer_1_out), .b(Input2), .eq(comparator_1_eq), .lt(comparator_1_lt));  // open: gt
  or or_2 (or_2_out, comparator_1_eq, comparator_1_lt);
  Multiplexer #(.enable("false")) multiplexer_2 (.in0(or_2_out), .in1(not_1_out), .out(BranchCond), .sel(BranchType));
  not not_1 (not_1_out, comparator_1_eq);
  Multiplexer #(.select(2), .width(16), .enable("false")) multiplexer_3 (
    .in0(adder_1_out), .in1(or_1_out), .in2(and_1_out), .out(Result), .sel(ALUOp));  // open: in3
endmodule

module Register (
  input  RegWrite,
  input  [2:0] Write_Register,
  input  [2:0] Read_Register_2,
  input  [2:0] Read_Register_1,
  input  [15:0] Write_Data,
  input  Halt,
  output [15:0] Read_Data_1,
  output [15:0] Read_Data_2
);

  wire and_1_out, and_2_out, and_3_out, and_4_out, and_5_out, and_6_out, and_7_out, and_8_out, clock_1_out,
       decoder_1_out0, decoder_1_out1, decoder_1_out2, decoder_1_out3, decoder_1_out4, decoder_1_out5,
       decoder_1_out6, decoder_1_out7, undriven;
  wire [15:0] register_1_q, register_2_q, register_3_q, register_4_q, register_5_q, register_6_q,
       register_7_q, register_8_q;

  Decoder #(.select(3), .enable("false")) decoder_1 (
    .out0(decoder_1_out0), .out1(decoder_1_out1), .out2(decoder_1_out2), .out3(decoder_1_out3),
    .out4(decoder_1_out4), .out5(decoder_1_out5), .out6(decoder_1_out6), .out7(decoder_1_out7),
    .sel(Write_Register));
  Clock clock_1 (.out(clock_1_out));
  and and_1 (and_1_out, RegWrite, Halt, decoder_1_out0);
  and and_2 (and_2_out, RegWrite, Halt, decoder_1_out1);
  and and_3 (and_3_out, RegWrite, Halt, decoder_1_out2);
  and and_4 (and_4_out, RegWrite, Halt, decoder_1_out3);
  and and_5 (and_5_out, RegWrite, Halt, decoder_1_out4);
  and and_6 (and_6_out, RegWrite, Halt, decoder_1_out5);
  and and_7 (and_7_out, RegWrite, Halt, decoder_1_out6);
  and and_8 (and_8_out, RegWrite, Halt, decoder_1_out7);
  Register_part #(.width(16)) register_1 (
    .D(Write_Data), .en(and_1_out), .Q(register_1_q), .clk(clock_1_out), .clr(undriven));
  Register_part #(.width(16)) register_2 (
    .D(Write_Data), .en(and_2_out), .Q(register_2_q), .clk(clock_1_out), .clr(undriven));
  Register_part #(.width(16)) register_3 (
    .D(Write_Data), .en(and_3_out), .Q(register_3_q), .clk(clock_1_out), .clr(undriven));
  Register_part #(.width(16)) register_4 (
    .D(Write_Data), .en(and_4_out), .Q(register_4_q), .clk(clock_1_out), .clr(undriven));
  Register_part #(.width(16)) register_5 (
    .D(Write_Data), .en(and_5_out), .Q(register_5_q), .clk(clock_1_out), .clr(undriven));
  Register_part #(.width(16)) register_6 (
    .D(Write_Data), .en(and_6_out), .Q(register_6_q), .clk(clock_1_out), .clr(undriven));
  Register_part #(.width(16)) register_7 (
    .D(Write_Data), .en(and_7_out), .Q(register_7_q), .clk(clock_1_out), .clr(undriven));
  Register_part #(.width(16)) register_8 (
    .D(Write_Data), .en(and_8_out), .Q(register_8_q), .clk(clock_1_out), .clr(undriven));
  Multiplexer #(.select(3), .width(16), .enable("false")) multiplexer_1 (
    .in0(register_1_q), .in1(register_2_q), .in2(register_3_q), .in3(register_4_q), .in4(register_5_q),
    .in5(register_6_q), .in6(register_7_q), .in7(register_8_q), .out(Read_Data_1), .sel(Read_Register_1));
  Multiplexer #(.select(3), .width(16), .enable("false")) multiplexer_2 (
    .in0(register_1_q), .in1(register_2_q), .in2(register_3_q), .in3(register_4_q), .in4(register_5_q),
    .in5(register_6_q), .in6(register_7_q), .in7(register_8_q), .out(Read_Data_2), .sel(Read_Register_2));
endmodule

module Fetch_Instructions (
  input  Halt,
  input  [15:0] Offset,
  input  Branch,
  input  BranchCond,
  input  Jump,
  input  [15:0] ra,
  input  Return,
  output [15:0] Address,
  output [15:0] Next
);

  wire and_1_out, clock_1_out, or_1_out;
  wire [15:0] adder_2_out, multiplexer_1_out, multiplexer_2_out;

  Clock clock_1 (.out(clock_1_out));
  Register_part #(.width(16)) PC (.D(multiplexer_1_out), .en(Halt), .Q(Address), .clk(clock_1_out));  // open: clr
  Adder #(.width(16)) adder_1 (.a(Address), .b(16'h1), .out(Next));  // open: cin, cout
  and and_1 (and_1_out, Branch, BranchCond);
  Multiplexer #(.width(16), .enable("false")) multiplexer_1 (
    .in0(multiplexer_2_out), .in1(ra), .out(multiplexer_1_out), .sel(Return));
  Adder #(.width(16)) adder_2 (.a(Address), .b(Offset), .out(adder_2_out));  // open: cin, cout
  or or_1 (or_1_out, and_1_out, Jump);
  Multiplexer #(.width(16), .enable("false")) multiplexer_2 (
    .in0(Next), .in1(adder_2_out), .out(multiplexer_2_out), .sel(or_1_out));
endmodule

module CPU (
);

  wire alu_1_branchcond, clock_1_out, clock_2_out, control_unit_1_alusrc, control_unit_1_branch,
       control_unit_1_branchtype, control_unit_1_call, control_unit_1_halt, control_unit_1_jump,
       control_unit_1_loadimm, control_unit_1_memread___memtoreg, control_unit_1_memwrite,
       control_unit_1_regdst, control_unit_1_regwrite, control_unit_1_return, not_1_out;
  wire [1:0] control_unit_1_aluop;
  wire [2:0] multiplexer_1_out;
  wire [15:0] alu_1_result, bit_extender_1_out, fetch_instructions_1_address, fetch_instructions_1_next,
       multiplexer_2_out, multiplexer_3_out, ra_q, ram_1_data, ram_2_data, register_1_read_data_1,
       register_1_read_data_2;

  not not_1 (not_1_out, control_unit_1_halt);
  RAM #(.addrWidth(16), .dataWidth(16)) ram_1 (
    .addr(fetch_instructions_1_address), .data(ram_1_data));  // open: sel, clk, ld, clr
  Fetch_Instructions fetch_instructions_1 (
    .Halt(not_1_out), .Offset(bit_extender_1_out), .Branch(alu_1_branchcond),
    .BranchCond(control_unit_1_branch), .Jump(control_unit_1_jump), .Address(fetch_instructions_1_address),
    .Next(fetch_instructions_1_next), .Return(control_unit_1_return), .ra(ra_q));
  Clock clock_1 (.out(clock_1_out));
  Register_part #(.width(16)) ra (
    .D(fetch_instructions_1_next), .en(control_unit_1_call), .Q(ra_q), .clk(clock_1_out));  // open: clr
  assign bit_extender_1_out = {{10{ram_1_data[15]}}, {ram_1_data[15:14], ram_1_data[7:4]}};  // Bit_Extender bit_extender_1
  Multiplexer #(.width(3), .enable("false")) multiplexer_1 (
    .in0(ram_1_data[10:8]), .in1(ram_1_data[7:5]), .out(multiplexer_1_out), .sel(control_unit_1_regdst));
  Register register_1 (
    .RegWrite(control_unit_1_regwrite), .Write_Register(multiplexer_1_out), .Write_Data(multiplexer_3_out),
    .Halt(not_1_out), .Read_Register_2(ram_1_data[10:8]), .Read_Register_1(ram_1_data[13:11]),
    .Read_Data_1(register_1_read_data_1), .Read_Data_2(register_1_read_data_2));
  Multiplexer #(.width(16), .enable("false")) multiplexer_2 (
    .in0(register_1_read_data_2), .in1(bit_extender_1_out), .out(multiplexer_2_out),
    .sel(control_unit_1_alusrc));
  Control_Unit control_unit_1 (
    .in_1(ram_1_data[3:0]), .RegWrite(control_unit_1_regwrite), .RegDst(control_unit_1_regdst),
    .ALUSrc(control_unit_1_alusrc), .MemWrite(control_unit_1_memwrite),
    .MemRead___MemToReg(control_unit_1_memread___memtoreg), .BranchType(control_unit_1_branchtype),
    .Branch(control_unit_1_branch), .ALUOp(control_unit_1_aluop), .Jump(control_unit_1_jump),
    .Call(control_unit_1_call), .Return(control_unit_1_return), .Halt(control_unit_1_halt),
    .LoadImm(control_unit_1_loadimm));
  Clock clock_2 (.out(clock_2_out));
  ALU alu_1 (
    .Input1(register_1_read_data_1), .Input2(multiplexer_2_out), .ALUOp(control_unit_1_aluop),
    .LoadImm(control_unit_1_loadimm), .BranchType(control_unit_1_branchtype), .Result(alu_1_result),
    .BranchCond(alu_1_branchcond));
  RAM #(.addrWidth(16), .dataWidth(16), .bus("separate")) ram_2 (
    .addr(alu_1_result), .din(register_1_read_data_2), .data(ram_2_data), .str(control_unit_1_memwrite),
    .clk(clock_2_out), .ld(control_unit_1_memread___memtoreg));  // open: sel, clr
  Multiplexer #(.width(16), .enable("false")) multiplexer_3 (
    .in0(alu_1_result), .in1(ram_2_data), .out(multiplexer_3_out), .sel(control_unit_1_memread___memtoreg));
endmodule

module Control_Unit (
  input  [3:0] in_1,
  output RegWrite,
  output RegDst,
  output ALUSrc,
  output MemWrite,
  output MemRead___MemToReg,
  output BranchType,
  output Branch,
  output [1:0] ALUOp,
  output Jump,
  output Call,
  output Return,
  output Halt,
  output LoadImm
);

  wire and_1_out, and_2_out, and_3_out, and_4_out, and_5_out, and_6_out, and_7_out, and_8_out, and_9_out,
       and_10_out, not_1_out, not_2_out, not_3_out, not_4_out, not_5_out, not_6_out, not_7_out, not_8_out,
       not_9_out, not_10_out, not_11_out, not_12_out, not_13_out, not_14_out, not_15_out, not_16_out,
       not_17_out, not_18_out, not_19_out, not_20_out, not_21_out, not_22_out, not_23_out, not_24_out,
       not_25_out, not_26_out, not_27_out, not_28_out, not_29_out;

  not not_1 (not_1_out, in_1[0]);
  not not_2 (not_2_out, in_1[2]);
  not not_3 (not_3_out, in_1[2]);
  not not_4 (not_4_out, in_1[3]);
  not not_5 (not_5_out, in_1[3]);
  not not_6 (not_6_out, in_1[1]);
  not not_7 (not_7_out, in_1[2]);
  not not_8 (not_8_out, in_1[0]);
  not not_9 (not_9_out, in_1[3]);
  not not_10 (not_10_out, in_1[1]);
  not not_11 (not_11_out, in_1[2]);
  not not_12 (not_12_out, in_1[3]);
  not not_13 (not_13_out, in_1[3]);
  not not_14 (not_14_out, in_1[1]);
  not not_15 (not_15_out, in_1[0]);
  not not_16 (not_16_out, in_1[2]);
  not not_17 (not_17_out, in_1[3]);
  and and_1 (and_1_out, not_1_out, in_1[1], not_2_out, in_1[3]);
  not not_18 (not_18_out, in_1[3]);
  and and_2 (and_2_out, in_1[1], not_3_out, in_1[3]);
  and and_3 (and_3_out, in_1[2], not_4_out);
  and and_4 (and_4_out, in_1[0], in_1[1], in_1[2], not_5_out);
  not not_19 (not_19_out, in_1[3]);
  and and_5 (and_5_out, not_6_out, not_7_out, in_1[3]);
  and and_6 (and_6_out, not_8_out, in_1[1], in_1[2], not_9_out);
  and and_7 (and_7_out, in_1[0], not_10_out, not_11_out, not_12_out);
  and and_8 (and_8_out, not_13_out, in_1[2], not_14_out, not_15_out);
  and and_9 (and_9_out, in_1[0], in_1[1], not_16_out, not_17_out);
  and and_10 (and_10_out, in_1[0], in_1[1], in_1[2], not_19_out);
  or or_1 (LoadImm, and_8_out, and_9_out);
  not not_20 (not_20_out, in_1[2]);
  not not_21 (not_21_out, in_1[3]);
  not not_22 (not_22_out, in_1[2]);
  not not_23 (not_23_out, in_1[0]);
  not not_24 (not_24_out, in_1[2]);
  not not_25 (not_25_out, in_1[1]);
  not not_26 (not_26_out, in_1[2]);
  not not_27 (not_27_out, in_1[1]);
  not not_28 (not_28_out, in_1[1]);
  not not_29 (not_29_out, in_1[0]);
  or or_2 (RegWrite, and_1_out, not_18_out);
  and and_11 (RegDst, not_20_out, not_21_out);
  or or_3 (ALUSrc, and_2_out, and_3_out);
  and and_12 (MemWrite, in_1[0], in_1[1], not_22_out, in_1[3]);
  and and_13 (MemRead___MemToReg, not_23_out, in_1[1], not_24_out, in_1[3]);
  and and_14 (Branch, not_25_out, not_26_out, in_1[3]);
  or or_4 (ALUOp[0], and_4_out, and_10_out, and_5_out);
  or or_5 (ALUOp[1], and_5_out, and_6_out, and_7_out);
  and and_15 (Jump, not_27_out, in_1[2], in_1[3]);
  and and_16 (Call, in_1[0], not_28_out, in_1[2], in_1[3]);
  and and_17 (Return, not_29_out, in_1[1], in_1[2], in_1[3]);
  and and_18 (Halt, in_1[0], in_1[1], in_1[2], in_1[3]);

  assign BranchType = in_1[0];
endmodule
